// Logisim project add-16.circ as structural Verilog: 5 circuits, main circuit main
module main (
  input  x1,
  input  x2,
  input  x3,
  input  x4,
  input  x5,
  input  x6,
  input  x7,
  input  x8,
  input  x9,
  input  x10,
  input  x11,
  input  x12,
  input  x13,
  input  x14,
  input  x15,
  input  x16,
  input  y1,
  input  y2,
  input  y3,
  input  y4,
  input  y5,
  input  y6,
  input  y7,
  input  y8,
  input  y9,
  input  y10,
  input  y11,
  input  y12,
  input  y13,
  input  y14,
  input  y15,
  input  y16,
  output o1,
  output o2,
  output o3,
  output o4,
  output _05,
  output o6,
  output o7,
  output o8,
  output o9,
  output o10,
  output o11,
  output o12,
  output o13,
  output o14,
  output o15,
  output o16,
  output out_49
);

  wire n4wei_1_jin, n4wei_2_jin, n4wei_3_jin;

  _4wei u_4wei_1 (
    .in(1'b0), .x1(x1), .x2(x2), .x3(x3), .x4(x4), .y1(y1), .y2(y2), .y3(y3), .y4(y4), .o1(o1), .o2(o2),
    .o3(o3), .o4(o4), .jin(n4wei_1_jin));
  _4wei u_4wei_2 (
    .in(n4wei_1_jin), .x1(x5), .x2(x6), .x3(x7), .x4(x8), .y1(y5), .y2(y6), .y3(y7), .y4(y8), .o1(_05),
    .o2(o6), .o3(o7), .o4(o8), .jin(n4wei_2_jin));
  _4wei u_4wei_3 (
    .in(n4wei_2_jin), .x1(x9), .x2(x10), .x3(x11), .x4(x12), .y1(y9), .y2(y10), .y3(y11), .y4(y12), .o1(o9),
    .o2(o10), .o3(o11), .o4(o12), .jin(n4wei_3_jin));
  _4wei u_4wei_4 (
    .in(n4wei_3_jin), .x1(x13), .x2(x14), .x3(x15), .x4(x16), .y1(y13), .y2(y14), .y3(y15), .y4(y16),
    .o1(o13), .o2(o14), .o3(o15), .o4(o16), .jin(out_49));
endmodule

module _4wei (
  input  in,
  input  x1,
  input  x2,
  input  x3,
  input  x4,
  input  y1,
  input  y2,
  input  y3,
  input  y4,
  output o1,
  output o2,
  output o3,
  output o4,
  output jin
);

  wire n1wei_1_c_out, n1wei_2_c_out, n1wei_3_c_out;

  _1wei u_1wei_1 (.A(x1), .B(y1), .C_in(in), .S(o1), .C_out(n1wei_1_c_out));
  _1wei u_1wei_2 (.A(x2), .B(y2), .C_in(n1wei_1_c_out), .S(o2), .C_out(n1wei_2_c_out));
  _1wei u_1wei_3 (.A(x3), .B(y3), .C_in(n1wei_2_c_out), .S(o3), .C_out(n1wei_3_c_out));
  _1wei u_1wei_4 (.A(x4), .B(y4), .C_in(n1wei_3_c_out), .S(o4), .C_out(jin));
endmodule

module _1wei (
  input  A,
  input  B,
  input  C_in,
  output S,
  output C_out
);

  wire and_1_out, and_2_out, and_3_out, and_4_out, and_5_out, and_6_out, and_7_out, not_1_out, not_2_out,
       not_3_out, not_4_out, not_5_out, not_6_out;

  not not_1 (not_1_out, A);
  not not_2 (not_2_out, B);
  not not_3 (not_3_out, A);
  not not_4 (not_4_out, C_in);
  not not_5 (not_5_out, B);
  not not_6 (not_6_out, C_in);
  and and_1 (and_1_out, B, C_in);
  and and_2 (and_2_out, A, C_in);
  and and_3 (and_3_out, A, B);
  and and_4 (and_4_out, not_1_out, not_2_out, C_in);
  and and_5 (and_5_out, not_3_out, B, not_4_out);
  and and_6 (and_6_out, A, not_5_out, not_6_out);
  and and_7 (and_7_out, A, B, C_in);
  or or_1 (C_out, and_1_out, and_2_out, and_3_out);
  or or_2 (S, and_4_out, and_5_out, and_6_out, and_7_out);
endmodule

module \_16_位二级先行进位加法器  (
  input  x1,
  input  x2,
  input  x3,
  input  x4,
  input  x5,
  input  x6,
  input  x7,
  input  x8,
  input  x9,
  input  x10,
  input  x11,
  input  x12,
  input  x13,
  input  x14,
  input  x15,
  input  x16,
  input  y1,
  input  y2,
  input  y3,
  input  y4,
  input  y5,
  input  y6,
  input  y7,
  input  y8,
  input  y9,
  input  y10,
  input  y11,
  input  y12,
  input  y13,
  input  y14,
  input  y15,
  input  y16,
  output o1,
  output o2,
  output o3,
  output o4,
  output _05,
  output o6,
  output o7,
  output o8,
  output o9,
  output o10,
  output o11,
  output o12,
  output o13,
  output o14,
  output o15,
  output o16,
  output out_49
);

  wire n4wei_1_jin, n4wei_2_jin, n4wei_3_jin;

  _4wei u_4wei_1 (
    .in(1'b0), .x1(x1), .x2(x2), .x3(x3), .x4(x4), .y1(y1), .y2(y2), .y3(y3), .y4(y4), .o1(o1), .o2(o2),
    .o3(o3), .o4(o4), .jin(n4wei_1_jin));
  _4wei u_4wei_2 (
    .in(n4wei_1_jin), .x1(x5), .x2(x6), .x3(x7), .x4(x8), .y1(y5), .y2(y6), .y3(y7), .y4(y8), .o1(_05),
    .o2(o6), .o3(o7), .o4(o8), .jin(n4wei_2_jin));
  _4wei u_4wei_3 (
    .in(n4wei_2_jin), .x1(x9), .x2(x10), .x3(x11), .x4(x12), .y1(y9), .y2(y10), .y3(y11), .y4(y12), .o1(o9),
    .o2(o10), .o3(o11), .o4(o12), .jin(n4wei_3_jin));
  _4wei u_4wei_4 (
    .in(n4wei_3_jin), .x1(x13), .x2(x14), .x3(x15), .x4(x16), .y1(y13), .y2(y14), .y3(y15), .y4(y16),
    .o1(o13), .o2(o14), .o3(o15), .o4(o16), .jin(out_49));
endmodule

module \串行进位加法器  (
  input  x1,
  input  x2,
  input  x3,
  input  x4,
  input  x5,
  input  x6,
  input  x7,
  input  x8,
  input  x9,
  input  x10,
  input  x11,
  input  x12,
  input  x13,
  input  x14,
  input  x15,
  input  x16,
  input  y1,
  input  y2,
  input  y3,
  input  y4,
  input  y5,
  input  y6,
  input  y7,
  input  y8,
  input  y9,
  input  y10,
  input  y11,
  input  y12,
  input  y13,
  input  y14,
  input  y15,
  input  y16,
  output o1,
  output o2,
  output o3,
  output o4,
  output _05,
  output o6,
  output o7,
  output o8,
  output o9,
  output o10,
  output o11,
  output o12,
  output o13,
  output o14,
  output o15,
  output o16,
  output out_49
);

  wire n1wei_1_c_out, n1wei_2_c_out, n1wei_3_c_out, n1wei_4_c_out, n1wei_5_c_out, n1wei_6_c_out,
       n1wei_7_c_out, n1wei_8_c_out, n1wei_9_c_out, n1wei_10_c_out, n1wei_11_c_out, n1wei_12_c_out,
       n1wei_13_c_out, n1wei_14_c_out, n1wei_15_c_out;

  _1wei u_1wei_1 (.A(1'b0), .B(x1), .C_in(y1), .S(o1), .C_out(n1wei_1_c_out));
  _1wei u_1wei_2 (.A(x2), .B(y2), .C_in(n1wei_1_c_out), .S(o2), .C_out(n1wei_2_c_out));
  _1wei u_1wei_3 (.A(x3), .B(y3), .C_in(n1wei_2_c_out), .S(o3), .C_out(n1wei_3_c_out));
  _1wei u_1wei_4 (.A(x4), .B(y4), .C_in(n1wei_3_c_out), .S(o4), .C_out(n1wei_4_c_out));
  _1wei u_1wei_5 (.A(x5), .B(y5), .C_in(n1wei_4_c_out), .S(_05), .C_out(n1wei_5_c_out));
  _1wei u_1wei_6 (.A(x6), .B(y6), .C_in(n1wei_5_c_out), .S(o6), .C_out(n1wei_6_c_out));
  _1wei u_1wei_7 (.A(x7), .B(y7), .C_in(n1wei_6_c_out), .S(o7), .C_out(n1wei_7_c_out));
  _1wei u_1wei_8 (.A(x8), .B(y8), .C_in(n1wei_7_c_out), .S(o8), .C_out(n1wei_8_c_out));
  _1wei u_1wei_9 (.A(x9), .B(y9), .C_in(n1wei_8_c_out), .S(o9), .C_out(n1wei_9_c_out));
  _1wei u_1wei_10 (.A(x10), .B(y10), .C_in(n1wei_9_c_out), .S(o10), .C_out(n1wei_10_c_out));
  _1wei u_1wei_11 (.A(x11), .B(y11), .C_in(n1wei_10_c_out), .S(o11), .C_out(n1wei_11_c_out));
  _1wei u_1wei_12 (.A(x12), .B(y12), .C_in(n1wei_11_c_out), .S(o12), .C_out(n1wei_12_c_out));
  _1wei u_1wei_13 (.A(x13), .B(y13), .C_in(n1wei_12_c_out), .S(o13), .C_out(n1wei_13_c_out));
  _1wei u_1wei_14 (.A(x14), .B(y14), .C_in(n1wei_13_c_out), .S(o14), .C_out(n1wei_14_c_out));
  _1wei u_1wei_15 (.A(x15), .B(y15), .C_in(n1wei_14_c_out), .S(o15), .C_out(n1wei_15_c_out));
  _1wei u_1wei_16 (.A(x16), .B(y16), .C_in(n1wei_15_c_out), .S(o16), .C_out(out_49));
endmodule
